// Logisim project control_logic.circ as structural Verilog: 1 circuit, main circuit control_logic
module control_logic (
  input  [31:0] inst,
  input  BrEq,
  input  BrLt,
  output PCSel,
  output RegWEn,
  output [2:0] ImmSel,
  output BrUn,
  output ASel,
  output BSel,
  output [3:0] ALUSel,
  output MemRW,
  output [1:0] WBSel,
  output CSRSel,
  output CSRWen
);

  wire and_1_out, and_2_out, and_3_out, and_4_out;

  and and_1 (and_1_out, inst[6], inst[5], ~inst[4], ~inst[2], inst[1], inst[0]);  // AND_Gate
  or or_1 (ImmSel[1], and_1_out, and_2_out, and_3_out);
  and and_2 (and_2_out, ~inst[6], ~inst[5], inst[4], inst[2], inst[1], inst[0]);  // AND_Gate
  and and_3 (and_3_out, ~inst[6], inst[5], inst[4], inst[2], inst[1], inst[0]);  // AND_Gate
  or or_2 (ImmSel[0], and_2_out, and_3_out, and_4_out);
  and and_4 (and_4_out, ~inst[6], inst[5], ~inst[4], ~inst[2], inst[1], inst[0]);  // AND_Gate

  assign ALUSel = 4'b0000;
  assign ImmSel[2] = inst[3];
  assign RegWEn = 1'b1;
  assign WBSel = 2'b00;

  // Other names for the same wires on the sheet: ImmSel2 = inst[3]; OP[6:0] = inst[6:0]

  // Notes on the sheet:
  //   INPUTS to your circuit
  //   ImmSel
  //   DON'T CHANGE THE LOCATIONS OF THE INPUTS AND OUTPUTS!
  //   OUTPUT from your circuit
endmodule
