// Logisim project cpu.circ as structural Verilog: 1 circuit, main circuit cpu
module cpu (
  input  clk,
  input  [31:0] INSTRUCTION,
  input  [31:0] READ_DATA,
  output [31:0] WRITE_ADDRESS,
  output [31:0] PROGRAM_COUNTER,
  output [31:0] ra,
  output [31:0] sp,
  output [31:0] t0,
  output [31:0] t1,
  output [31:0] t2,
  output [31:0] s0,
  output [31:0] s1,
  output [31:0] a0,
  output [31:0] tohost,
  output [3:0] WRITE_ENABLE,
  output [31:0] WRITE_DATA
);

  wire ASel, BrEq, BrLt, BrUn, BSel, csr_1_p1, csr_1_p3, csr_1_p5, CSRSel, CSRWen, MemRW, PCSel, RegWEn;
  wire [1:0] WBSel;
  wire [2:0] ImmSel;
  wire [3:0] ALUSel;
  wire [31:0] adder_1_out, ALURes, data1, imm, PC4, PIPED_INST, Write_Data_t;

  Adder #(.width(32)) adder_1 (.a(PROGRAM_COUNTER), .b(32'h4), .out(adder_1_out));  // open: cin, cout
  Register #(.width(32)) register_1 (.D(INSTRUCTION), .clk(clk), .Q(PIPED_INST));  // open: en, clr
  Register #(.width(32)) PC (.D(adder_1_out), .clk(clk), .Q(PROGRAM_COUNTER));  // open: en, clr
  control_logic control_logic_1 (
    .CSRWen(CSRWen), .PCSel(PCSel), .RegWEn(RegWEn), .ImmSel(ImmSel), .BrUn(BrUn), .ASel(ASel), .BSel(BSel),
    .ALUSel(ALUSel), .MemRW(MemRW), .WBSel(WBSel), .CSRSel(CSRSel), .inst(PIPED_INST), .BrEq(BrEq),
    .BrLt(BrLt));
  imm_gen imm_gen_1 (.inst(PIPED_INST), .ImmSel(ImmSel), .imm(imm));
  Multiplexer #(.enable("false"), .select(2), .width(32)) multiplexer_1 (
    .in0(ALURes), .in2(PC4), .in3(READ_DATA), .out(Write_Data_t), .sel(WBSel));  // open: in1
  regfile regfile_1 (
    .rs1(PIPED_INST[19:15]), .rd(PIPED_INST[11:7]), .Write_Data(Write_Data_t), .RegWEn(RegWEn), .clk(clk),
    .ra(ra), .sp(sp), .t0(t0), .t1(t1), .t2(t2), .s0(s0), .s1(s1), .a0(a0), .Read_Data_1(data1));  // open: rs2, Read_Data_2
  // branch_comp branch_comp_1: pin names not known
  alu alu_1 (.Result(ALURes), .A(data1), .B(imm), .ALUSel(ALUSel));
  // csr csr_1: pin names not known; wires that end beside it: csr_1_p1, csr_1_p1, csr_1_p3, csr_1_p3, csr_1_p5, tohost

  // Other names for the same wires on the sheet: rd[4:0] = PIPED_INST[11:7]; rs1[4:0] = PIPED_INST[19:15]

  // Notes on the sheet:
  //   Output to IMEM
  //   IMEM (do **NOT** move this)
  //   Inputs from IMEM
  //   It is OK to move the PC, RegFile, ALU, MEM, Branch Comp, Imm Gen, and Control Logic to wherever is most convenient for you when constructing your CPU, and to delete this text
  //   Inputs/Outputs for testing. Do **NOT** move these.
  //   Outputs To DMEM
  //   DMEM (do **NOT** move this)
  //   Inputs From DMEM
endmodule
